# Fritzing sketch Digispark-LCD (saved by Fritzing 0.9.3b)
breadboards: 1

parts:
  Digispark1 = Digispark
  LCM1602_IIC1 = LCM1602 IIC [part_number="LCM1602 IIC" chip_label="LCM1602 IIC" package="DIP (Dual Inline) [THT]"]
  R1 = Resistor [tolerance=±5% resistance=4.7k package=THT]
  R2 = Resistor [tolerance=±5% resistance=4.7k package=THT]
  LCD1 = LCD screen

nets:
  VCC: Digispark1.VCC, LCM1602_IIC1.VCC, R1.Pin_1, R2.Pin_1
  GND: Digispark1.GND, LCM1602_IIC1.GND
  N1: Digispark1.P0, LCM1602_IIC1.SDA, R2.Pin_0
  N2: Digispark1.P2, LCM1602_IIC1.SCL, R1.Pin_0
  VSS: LCM1602_IIC1.VSS, LCD1.VSS
  VDD: LCM1602_IIC1.VDD, LCD1.VDD
  N3: LCM1602_IIC1.V0, LCD1.V0
  N4: LCM1602_IIC1.RS, LCD1.RS
  N5: LCM1602_IIC1.RW, LCD1.R/W
  N6: LCM1602_IIC1.E, LCD1.E
  N7: LCM1602_IIC1.D0, LCD1.DB0
  N8: LCM1602_IIC1.D1, LCD1.DB1
  N9: LCM1602_IIC1.D2, LCD1.DB2
  N10: LCM1602_IIC1.D3, LCD1.DB3
  N11: LCM1602_IIC1.D4, LCD1.DB4
  N12: LCM1602_IIC1.D5, LCD1.DB5
  N13: LCM1602_IIC1.D6, LCD1.DB6
  N14: LCM1602_IIC1.D7, LCD1.DB7
  N15: LCM1602_IIC1.A, LCD1.LED+
  N16: LCM1602_IIC1.K, LCD1.LED-

custom parts:
  Digispark: The Digispark is an Attiny85 based microcontroller development board similar to the Arduino line, only cheaper, smaller, and a bit less powerful. With a whole host of shields to extend its functionality and the ability to use the familiar Arduino IDE the Digispark is a great way to jump into electronics, or perfect for when an Arduino is too big or too much.
  LCM1602 IIC: I2C-Module to use a 1602 or 2004 LCD on with the wire.h libory Serial LCD Modul
