# Fritzing sketch RC5 Sketch (saved by Fritzing 0.9.3b)
breadboards: 1

parts:
  IR1 = TSOP312.., 314.. [package=THT]
  LED1 = LED - 3mm [color="Red (633nm)" package="3 mm [THT]"]
  Digispark1 = Digispark
  R1 = Resistor [tolerance=±5% resistance=220 package=THT]

nets:
  GND: IR1.GND, LED1.cathode, Digispark1.GND
  N1: IR1.Vs, Digispark1.VCC
  N2: IR1.Data, Digispark1.P0
  N3: LED1.anode, R1.Pin_0
  N4: Digispark1.P1, R1.Pin_1

custom parts:
  Digispark: The Digispark is an Attiny85 based microcontroller development board similar to the Arduino line, only cheaper, smaller, and a bit less powerful. With a whole host of shields to extend its functionality and the ability to use the familiar Arduino IDE the Digispark is a great way to jump into electronics, or perfect for when an Arduino is too big or too much.
