# Fritzing sketch ESP-OLED (saved by Fritzing 0.9.3b)
breadboards: 1

parts:
  U1 = NodeMCU V1.0
  Squix1 = OLED 0.96" 128x64 I2C SSD1306
  S1 = Pushbutton [package="[THT]"]
  S2 = Pushbutton [package="[THT]"]
  S3 = Pushbutton [package="[THT]"]
  Q1 = NPN-Transistor [package="TO92 [THT]"]
  R1 = Resistor [tolerance=±5% resistance=4.7k package=THT]
  R2 = Resistor [tolerance=±5% resistance=470 package=THT]
  R3 = Resistor [tolerance=±5% resistance=470 package=THT]
  R4 = Resistor [tolerance=±5% resistance=470 package=THT]
  Part1 = CEM-1203(42) Magnetic Buzzer Module [package="Breakout board"]

nets:
  N1: U1.D1, Squix1.SCL
  N2: U1.D2, Squix1.SCA
  N3: U1.D3, R1.Pin_1
  3V3: U1.3V3, Squix1.VCC, Part1.+
  GND: U1.GND, Squix1.GND, S1.Pin_3, S1.Pin_4, S2.Pin_3, S2.Pin_4, S3.Pin_3, S3.Pin_4, Q1.E
  N4: U1.D5, R2.Pin_1
  N5: U1.D6, R3.Pin_1
  N6: U1.D7, R4.Pin_1
  N7: S1.Pin_1, S1.Pin_2, R2.Pin_0
  N8: S2.Pin_1, S2.Pin_2, R3.Pin_0
  N9: S3.Pin_1, S3.Pin_2, R4.Pin_0
  N10: Q1.B, R1.Pin_0
  N11: Q1.C, Part1.-

custom parts:
  NodeMCU V1.0: ESP8266 based NodeMCU
  CEM-1203(42) Magnetic Buzzer Module: Magnetic Buzzer Module CEM1203(42), it can produce a range of sound tones depending on the input frequency.
