# Fritzing sketch RFID_reader_RDM6300 (saved by Fritzing 0.9.3b)

parts:
  125_kHz_RFID_module1 = RDM6300
  Součástka2 = RDM6300-ANT  # not connected
  Součástka1 = USB converter CP2102

nets:
  N1: 125_kHz_RFID_module1.TX, Součástka1.RXI
  GND: 125_kHz_RFID_module1.GND, Součástka1.GND
  +5V: 125_kHz_RFID_module1.+5V, Součástka1.+5V

custom parts:
  RDM6300: 125 kHz RFID module (serial interface)
  RDM6300-ANT: Antenna
